// Logisim project computer.circ as structural Verilog: 10 circuits, main circuit main
module main (
  input  Clear,
  output [15:0] out_2
);

  wire and_1_out, clock_1_out, instructiondecoder_1_jmp, instructiondecoder_1_writeram, jmpinst_1_jmp,
       registers_1_p5, registers_1_p6, registers_1_p7;
  wire [15:0] alu_1_outval, jmpinst_1_jmpval, meminst_1_memval, meminst_1_ramaddr, programcounter_1_ip,
       registers_1_p4, registers_1_p10, registers_1_p11, registers_1_p12, registers_1_p13;
  wire [31:0] rom_1_data;

  Clock clock_1 (.out(clock_1_out));
  ROM #(.addrWidth(16), .dataWidth(32)) rom_1 (.addr(programcounter_1_ip), .data(rom_1_data));
  ProgramCounter programcounter_1 (
    .JmpAddr(registers_1_p4), .Reset(Clear), .Jmp(and_1_out), .Clock(clock_1_out), .ip(programcounter_1_ip));
  RAM #(.addrWidth(16), .asyncread("true"), .clearpin("true"), .dataWidth(16)) ram_1 (
    .addr(meminst_1_ramaddr), .we(instructiondecoder_1_writeram), .oe(1'b1), .clk(clock_1_out),
    .din(registers_1_p4), .dout(out_2), .clr(Clear));
  // Registers registers_1: pin names not known; wires that end beside it: rom_1_data[7:0], rom_1_data[15:8], rom_1_data[23:16], registers_1_p4, registers_1_p5, registers_1_p6, registers_1_p7, clock_1_out, Clear, registers_1_p10, registers_1_p11, registers_1_p12, registers_1_p13
  JmpInst jmpinst_1 (
    .JmpVal(jmpinst_1_jmpval), .Jmp(jmpinst_1_jmp), .Areg(registers_1_p10), .OpCode(rom_1_data[31:24]),
    .Breg(registers_1_p11), .Creg(registers_1_p12), .A(rom_1_data[23:16]), .B(rom_1_data[15:8]),
    .C(rom_1_data[7:0]));
  MemInst meminst_1 (
    .MemVal(meminst_1_memval), .RamAddr(meminst_1_ramaddr), .AReg(registers_1_p10), .Breg(registers_1_p11),
    .Creg(registers_1_p12), .RamVal(out_2), .StackPtr(registers_1_p13), .OpCode(rom_1_data[31:24]),
    .A(rom_1_data[23:16]), .B(rom_1_data[15:8]), .C(rom_1_data[7:0]));
  ALU alu_1 (.OpCode(rom_1_data[31:24]), .B(registers_1_p11), .C(registers_1_p12), .OutVal(alu_1_outval));
  InstructionDecoder instructiondecoder_1 (
    .WriteRegister(registers_1_p5), .Jmp(instructiondecoder_1_jmp), .WriteRAM(instructiondecoder_1_writeram),
    .DecrementSP(registers_1_p7), .IncrementSP(registers_1_p6), .OutVal(registers_1_p4),
    .JmpVal(jmpinst_1_jmpval), .ALUval(alu_1_outval), .OpCode(rom_1_data[31:24]), .MemoryVal(meminst_1_memval));
  and and_1 (and_1_out, jmpinst_1_jmp, instructiondecoder_1_jmp);

  // Notes on the sheet:
  //   contents of rom_1 (hex, n*v repeats v):
  //   4002beef 46020000 30000100
endmodule

module Registers (
  input  [7:0] Aaddr,
  input  [7:0] Baddr,
  input  [7:0] Caddr,
  input  [15:0] InValue,
  input  writeEnabled,
  input  IncSP,
  input  DecSP,
  input  Clock,
  input  Clear,
  output [15:0] Aout,
  output [15:0] Bout,
  output [15:0] Cout,
  output [15:0] StackPtr
);

  wire buffer_1_out, buffer_2_out, buffer_3_out, demultiplexer_1_out0, demultiplexer_1_out1,
       demultiplexer_1_out2, demultiplexer_1_out3, demultiplexer_1_out4, demultiplexer_1_out5,
       demultiplexer_1_out6, demultiplexer_1_out7, or_2_out, or_3_out;
  wire [15:0] adder_1_out, multiplexer_1_out, multiplexer_2_out, or_1_out, register_1_q, register_2_q,
       register_3_q, register_4_q, register_5_q, register_6_q, register_7_q, subtractor_1_out, widen_1_out_2;

  Adder #(.width(16)) adder_1 (.a(StackPtr), .b(16'h1), .out(adder_1_out));  // open: cin, cout
  Subtractor #(.width(16)) subtractor_1 (.a(StackPtr), .b(16'h1), .out(subtractor_1_out));  // open: bin, bout
  Demultiplexer #(.enable("false"), .select(3)) demultiplexer_1 (
    .out0(demultiplexer_1_out0), .out1(demultiplexer_1_out1), .out2(demultiplexer_1_out2),
    .out3(demultiplexer_1_out3), .out4(demultiplexer_1_out4), .out5(demultiplexer_1_out5),
    .out6(demultiplexer_1_out6), .out7(demultiplexer_1_out7), .in(writeEnabled), .sel(Aaddr[2:0]));
  Multiplexer #(.enable("false"), .width(16)) multiplexer_1 (
    .in0(InValue), .in1(adder_1_out), .out(multiplexer_1_out), .sel(IncSP));
  Multiplexer #(.enable("false"), .width(16)) multiplexer_2 (
    .in0(multiplexer_1_out), .in1(subtractor_1_out), .out(multiplexer_2_out), .sel(DecSP));
  Widen widen_1 (.out_2(widen_1_out_2), .in_1(Clear));
  assign or_1_out = widen_1_out_2 | multiplexer_2_out;  // OR_Gate or_1, 16 bits wide
  or or_2 (or_2_out, Clear, demultiplexer_1_out7, DecSP, IncSP);
  Register #(.width(16)) register_1 (
    .D(InValue), .en(demultiplexer_1_out0), .Q(register_1_q), .clk(Clock), .clr(Clear));
  Register #(.width(16)) register_2 (
    .D(InValue), .en(demultiplexer_1_out1), .Q(register_2_q), .clk(Clock), .clr(Clear));
  Register #(.width(16)) register_3 (
    .D(InValue), .en(demultiplexer_1_out2), .Q(register_3_q), .clk(Clock), .clr(Clear));
  Register #(.width(16)) register_4 (
    .D(InValue), .en(demultiplexer_1_out3), .Q(register_4_q), .clk(Clock), .clr(Clear));
  Register #(.width(16)) register_5 (
    .D(InValue), .en(demultiplexer_1_out4), .Q(register_5_q), .clk(Clock), .clr(Clear));
  Register #(.width(16)) register_6 (
    .D(InValue), .en(demultiplexer_1_out5), .Q(register_6_q), .clk(Clock), .clr(Clear));
  Register #(.width(16)) register_7 (
    .D(InValue), .en(demultiplexer_1_out6), .Q(register_7_q), .clk(Clock), .clr(Clear));
  Register #(.width(16)) register_8 (.D(or_1_out), .en(or_2_out), .Q(StackPtr), .clk(buffer_1_out));  // open: clr
  buf buffer_1 (buffer_1_out, buffer_2_out);
  buf buffer_2 (buffer_2_out, buffer_3_out);
  buf buffer_3 (buffer_3_out, or_3_out);
  or or_3 (or_3_out, Clock, Clear);
  Multiplexer #(.enable("false"), .select(3), .width(16)) multiplexer_3 (
    .in0(register_1_q), .in1(register_2_q), .in2(register_3_q), .in3(register_4_q), .in4(register_5_q),
    .in5(register_6_q), .in6(register_7_q), .in7(StackPtr), .out(Aout), .sel(Aaddr[2:0]));
  Multiplexer #(.enable("false"), .select(3), .width(16)) multiplexer_4 (
    .in0(register_1_q), .in1(register_2_q), .in2(register_3_q), .in3(register_4_q), .in4(register_5_q),
    .in5(register_6_q), .in6(register_7_q), .in7(StackPtr), .out(Bout), .sel(Baddr[2:0]));
  Multiplexer #(.enable("false"), .select(3), .width(16)) multiplexer_5 (
    .in0(register_1_q), .in1(register_2_q), .in2(register_3_q), .in3(register_4_q), .in4(register_5_q),
    .in5(register_6_q), .in6(register_7_q), .in7(StackPtr), .out(Cout), .sel(Caddr[2:0]));
endmodule

module ALU (
  input  [7:0] OpCode,
  input  [15:0] B,
  input  [15:0] C,
  output [15:0] OutVal
);

  wire comparator_1_eq, comparator_1_gt, comparator_1_lt, not_2_out, not_3_out, not_4_out, or_2_out, or_3_out;
  wire [15:0] adder_1_out, and_1_out, divider_1_out, divider_1_rem, multiplexer_1_out, multiplexer_2_out,
       multiplier_1_out, not_1_out, onetosixteen_1_out_2, onetosixteen_2_out_2, onetosixteen_3_out_2,
       onetosixteen_4_out_2, onetosixteen_5_out_2, onetosixteen_6_out_2, or_1_out, subtractor_1_out,
       xor_1_out;

  Adder #(.width(16)) adder_1 (.a(B), .b(C), .out(adder_1_out));  // open: cin, cout
  Subtractor #(.width(16)) subtractor_1 (.a(B), .b(C), .out(subtractor_1_out));  // open: bin, bout
  Multiplier #(.width(16)) multiplier_1 (.a(B), .b(C), .out(multiplier_1_out));  // open: cin, cout
  Divider #(.width(16)) divider_1 (.a(B), .b(C), .out(divider_1_out), .rem(divider_1_rem));  // open: upper
  assign not_1_out = ~B;  // NOT_Gate not_1, 16 bits wide
  assign and_1_out = B & C;  // AND_Gate and_1, 16 bits wide
  assign or_1_out = B | C;  // OR_Gate or_1, 16 bits wide
  assign xor_1_out = B ^ C;  // XOR_Gate xor_1, 16 bits wide
  Comparator #(.width(16)) comparator_1 (
    .a(B), .b(C), .gt(comparator_1_gt), .eq(comparator_1_eq), .lt(comparator_1_lt));
  or or_2 (or_2_out, comparator_1_gt, comparator_1_eq);
  or or_3 (or_3_out, comparator_1_eq, comparator_1_lt);
  OneToSixteen onetosixteen_1 (.out_2(onetosixteen_1_out_2), .in_1(comparator_1_eq));
  not not_2 (not_2_out, comparator_1_eq);
  OneToSixteen onetosixteen_2 (.out_2(onetosixteen_2_out_2), .in_1(not_2_out));
  OneToSixteen onetosixteen_3 (.out_2(onetosixteen_3_out_2), .in_1(or_2_out));
  OneToSixteen onetosixteen_4 (.out_2(onetosixteen_4_out_2), .in_1(or_3_out));
  not not_3 (not_3_out, or_3_out);
  OneToSixteen onetosixteen_5 (.out_2(onetosixteen_5_out_2), .in_1(not_3_out));
  not not_4 (not_4_out, or_2_out);
  OneToSixteen onetosixteen_6 (.out_2(onetosixteen_6_out_2), .in_1(not_4_out));
  Multiplexer #(.enable("false"), .select(4), .width(16)) multiplexer_1 (
    .in0(adder_1_out), .in1(subtractor_1_out), .in2(multiplier_1_out), .in3(divider_1_out),
    .in4(divider_1_rem), .in5({16{1'b0}}), .in6({16{1'b0}}), .in7({16{1'b0}}), .in8({16{1'b0}}),
    .in9({16{1'b0}}), .in10({16{1'b0}}), .in11({16{1'b0}}), .in12({16{1'b0}}), .in13({16{1'b0}}),
    .in14({16{1'b0}}), .in15({16{1'b0}}), .out(multiplexer_1_out), .sel(OpCode[3:0]));
  Multiplexer #(.enable("false"), .select(4), .width(16)) multiplexer_2 (
    .in0(not_1_out), .in1(and_1_out), .in2(or_1_out), .in3(xor_1_out), .in4(onetosixteen_1_out_2),
    .in5(onetosixteen_2_out_2), .in6(onetosixteen_3_out_2), .in7(onetosixteen_4_out_2),
    .in8(onetosixteen_5_out_2), .in9(onetosixteen_6_out_2), .in10({16{1'b0}}), .in11({16{1'b0}}),
    .in12({16{1'b0}}), .in13({16{1'b0}}), .in14({16{1'b0}}), .in15({16{1'b0}}), .out(multiplexer_2_out),
    .sel(OpCode[3:0]));
  Multiplexer #(.enable("false"), .width(16)) multiplexer_3 (
    .in0(multiplexer_1_out), .in1(multiplexer_2_out), .out(OutVal), .sel(OpCode[5]));
endmodule

module OneToSixteen (
  input  in_1,
  output [15:0] out_2
);


  assign out_2 = {{15{1'b0}}, in_1};
endmodule

module InstructionDecoder (
  input  [7:0] OpCode,
  input  [15:0] JmpVal,
  input  [15:0] ALUval,
  input  [15:0] MemoryVal,
  output WriteRegister,
  output Jmp,
  output WriteRAM,
  output DecrementSP,
  output IncrementSP,
  output [15:0] OutVal
);

  wire and_2_out, and_3_out, and_4_out, and_5_out, nor_1_out, xor_1_out;
  wire [15:0] multiplexer_1_out;

  xor xor_1 (xor_1_out, OpCode[4], OpCode[5]);
  nor nor_1 (nor_1_out, OpCode[6], OpCode[7]);
  and and_1 (Jmp, OpCode[4], OpCode[5], ~OpCode[6], ~OpCode[7]);  // AND_Gate
  and and_2 (and_2_out, ~OpCode[4], ~OpCode[5], OpCode[6], ~OpCode[7]);  // AND_Gate
  and and_3 (and_3_out, xor_1_out, nor_1_out);
  and and_4 (and_4_out, and_2_out, ~OpCode[2], ~OpCode[3]);  // AND_Gate
  and and_5 (and_5_out, and_2_out, ~OpCode[1], OpCode[2], ~OpCode[3]);  // AND_Gate
  and and_6 (DecrementSP, and_2_out, ~OpCode[0], OpCode[1], OpCode[2], ~OpCode[3]);  // AND_Gate
  and and_7 (IncrementSP, and_2_out, OpCode[0], OpCode[1], OpCode[2], ~OpCode[3]);  // AND_Gate
  Multiplexer #(.enable("false"), .width(16)) multiplexer_1 (
    .in0(ALUval), .in1(MemoryVal), .out(multiplexer_1_out), .sel(and_2_out));
  Multiplexer #(.enable("false"), .width(16)) multiplexer_2 (
    .in0(multiplexer_1_out), .in1(JmpVal), .out(OutVal), .sel(Jmp));
  or or_1 (WriteRegister, and_3_out, IncrementSP, and_4_out);
  or or_2 (WriteRAM, and_5_out, DecrementSP);

  // Notes on the sheet:
  //   category:
  //   instruction:
  //   isALU
  //   isFlowControl
  //   isMemory
  //   isStr(i)
  //   isPush
  //   isPop
  //   isSetCopyLoad(i)
endmodule

module ProgramCounter (
  input  [15:0] JmpAddr,
  input  Reset,
  input  Jmp,
  input  Clock,
  output [15:0] ip
);

  wire [15:0] adder_1_out, multiplexer_1_out;

  Adder #(.width(16)) adder_1 (.a(ip), .b(16'h1), .out(adder_1_out));  // open: cin, cout
  Multiplexer #(.enable("false"), .width(16)) multiplexer_1 (
    .in0(adder_1_out), .in1(JmpAddr), .out(multiplexer_1_out), .sel(Jmp));
  Register #(.width(16)) register_1 (.D(multiplexer_1_out), .en(1'b1), .Q(ip), .clk(Clock), .clr(Reset));
endmodule

module JmpInst (
  input  [7:0] OpCode,
  input  [7:0] A,
  input  [7:0] B,
  input  [7:0] C,
  input  [15:0] Areg,
  input  [15:0] Breg,
  input  [15:0] Creg,
  output [15:0] JmpVal,
  output Jmp
);

  wire comparator_1_eq, comparator_2_eq, not_1_out, not_2_out;

  not not_1 (not_1_out, comparator_1_eq);
  Comparator #(.width(16)) comparator_1 (.a({16{1'b0}}), .b(Creg), .eq(comparator_1_eq));  // open: gt, lt
  not not_2 (not_2_out, comparator_2_eq);
  Comparator #(.width(16)) comparator_2 (.a(Breg), .b({16{1'b0}}), .eq(comparator_2_eq));  // open: gt, lt
  Multiplexer #(.enable("false"), .select(2), .width(16)) multiplexer_1 (
    .in0({A, B}), .in1(Areg), .in2({A, B}), .in3(Areg), .out(JmpVal), .sel(OpCode[1:0]));
  Multiplexer #(.enable("false"), .select(2)) multiplexer_2 (
    .in0(1'b1), .in1(1'b1), .in2(not_1_out), .in3(not_2_out), .out(Jmp), .sel(OpCode[1:0]));
endmodule

module CPU (
  input  in_1
);

  wire [15:0] alu_1_outval, programcounter_1_ip, registers_1_bout, registers_1_cout;
  wire [31:0] rom_1_data;

  RAM #(.addrWidth(16), .dataWidth(16)) ram_1 ();  // open: addr, we, oe, clk, din, dout
  ROM #(.addrWidth(16), .dataWidth(32)) rom_1 (.addr(programcounter_1_ip), .data(rom_1_data));
  ProgramCounter programcounter_1 (.ip(programcounter_1_ip));  // open: JmpAddr, Reset, Jmp, Clock
  Registers registers_1 (
    .Bout(registers_1_bout), .Cout(registers_1_cout), .writeEnabled(in_1), .InValue(alu_1_outval),
    .Aaddr(rom_1_data[23:16]), .Baddr(rom_1_data[15:8]), .Caddr(rom_1_data[7:0]));  // open: Aout, StackPtr, IncSP, DecSP, Clock, Clear
  ALU alu_1 (.OpCode(rom_1_data[31:24]), .B(registers_1_bout), .C(registers_1_cout), .OutVal(alu_1_outval));

  // Notes on the sheet:
  //   contents of rom_1 (hex, n*v repeats v):
  //   1 3 2 1
endmodule

module MemInst (
  input  [7:0] OpCode,
  input  [7:0] A,
  input  [7:0] B,
  input  [7:0] C,
  input  [15:0] AReg,
  input  [15:0] Breg,
  input  [15:0] Creg,
  input  [15:0] RamVal,
  input  [15:0] StackPtr,
  output [15:0] MemVal,
  output [15:0] RamAddr
);

  wire [15:0] subtractor_1_out;

  Subtractor #(.width(16)) subtractor_1 (.a(StackPtr), .b(16'h1), .out(subtractor_1_out));  // open: bin, bout
  Multiplexer #(.enable("false"), .select(3), .width(16)) multiplexer_1 (
    .in0({B, C}), .in1(Breg), .in2(RamVal), .in3(RamVal), .in4(Creg), .in5(Breg), .in6(AReg), .in7(RamVal),
    .out(MemVal), .sel(OpCode[2:0]));
  Multiplexer #(.enable("false"), .select(3), .width(16)) multiplexer_2 (
    .in0({16{1'b0}}), .in1({16{1'b0}}), .in2({B, C}), .in3(Breg), .in4({A, B}), .in5(AReg), .in6(StackPtr),
    .in7(subtractor_1_out), .out(RamAddr), .sel(OpCode[2:0]));
endmodule

module Widen (
  input  in_1,
  output [15:0] out_2
);


  assign out_2 = {16{in_1}};
endmodule
